# Fritzing sketch Q4 (saved by Fritzing 0.9.3b)
breadboards: 1

parts:
  Part1 = Arduino Uno (Rev3)
  R1 = Rotary Potentiometer (Small) [maximum_resistance=100kΩ package=THT]
  J1 = Basic Servo
  R2 = Rotary Potentiometer (Small) [maximum_resistance=100kΩ package=THT]

nets:
  N1: Part1.A0, R1.wiper
  N2: Part1.A1, R2.wiper
  N3: Part1.D11_PWM/MOSI, J1.pulse
  5V: Part1.5V, R1.leg2, J1.vcc, R2.leg2
  GND: Part1.GND, R1.leg1, J1.gnd, R2.leg1
