# Fritzing sketch Q3 (saved by Fritzing 0.9.3b)
breadboards: 1

parts:
  Part1 = Arduino Uno (Rev3)
  S1 = Pushbutton [package="[THT]"]
  S2 = Pushbutton [package="[THT]"]
  R2 = Resistor [tolerance=±5% resistance=10k package=THT]
  R3 = Resistor [tolerance=±5% resistance=10k package=THT]
  LED1 = LED - 5mm [color="Red (633nm)" package="5 mm [THT]"]
  LED2 = LED - 5mm [color="Red (633nm)" package="5 mm [THT]"]
  R4 = Resistor [tolerance=±5% resistance=470k package=THT]
  R5 = Resistor [tolerance=±5% resistance=470k package=THT]

nets:
  N1: Part1.D2, LED1.anode
  N2: Part1.D4, LED2.anode
  N3: Part1.D5_PWM, S2.Pin_3, S2.Pin_4, R3.Pin_0
  N4: Part1.D6_PWM, S1.Pin_3, S1.Pin_4, R2.Pin_0
  N5: Part1.5V, S1.Pin_1, S1.Pin_2, S2.Pin_1, S2.Pin_2
  N6: Part1.GND, R2.Pin_1, R3.Pin_1, R4.Pin_1, R5.Pin_1
  N7: LED1.cathode, R5.Pin_0
  N8: LED2.cathode, R4.Pin_0
