# Fritzing sketch Untitled Sketch (saved by Fritzing 0.9.3b)
breadboards: 1

parts:
  Raspberry_Pi_1 = Raspberry Pi 3 [part_number=RPI-3-V1.2]
  LED1 = LED - 5mm [color="Red (633nm)" package="5 mm [THT]"]
  LED2 = LED - 5mm [color="Red (633nm)" package="5 mm [THT]"]
  LED3 = LED - 5mm [color="Red (633nm)" package="5 mm [THT]"]
  S1 = Pushbutton [package="[THT]"]

nets:
  N1: Raspberry_Pi_1.3v3, S1.Pin_1, S1.Pin_2
  N2: Raspberry_Pi_1.GIPO20, S1.Pin_3, S1.Pin_4
  N3: Raspberry_Pi_1.GIPO12, LED3.anode
  N4: Raspberry_Pi_1.GIPO25, LED2.anode
  N5: Raspberry_Pi_1.GIPO23, LED1.anode
  N6: Raspberry_Pi_1.GND, LED1.cathode, LED2.cathode, LED3.cathode
